# Fritzing sketch board (saved by Fritzing 0.9.3b)
circuit board: 6.88566cm x 5.36311cm
breadboards: 1
perfboards: 1

parts:
  Part1 = Arduino Uno (Rev3)
  S1 = SWITCH-DPDT [package=os]
  J1 = female pin header, 6 pins [form="♀ (female)"]
  S2 = SPST Switch [package=switch-spdt]
  J2 = female pin header, 5 pins [form="♀ (female)"]
  Adafruit_HUZZAH_ESP8266_Breakout1 = Adafruit HUZZAH ESP8266 Breakout [part_number=2471]
  J3 = female pin header, 5 pins [form="♀ (female)"]  # not connected
  J4 = female pin header, 5 pins [form="♀ (female)"]  # not connected
  J5 = female pin header, 5 pins [form="♀ (female)"]  # not connected
  J6 = female pin header, 5 pins [form="♀ (female)"]  # not connected
  J7 = female pin header, 5 pins [form="♀ (female)"]  # not connected
  J8 = female pin header, 5 pins [form="♀ (female)"]  # not connected
  J9 = female pin header, 5 pins [form="♀ (female)"]  # not connected
  J10 = female pin header, 5 pins [form="♀ (female)"]  # not connected
  J11 = female pin header, 5 pins [form="♀ (female)"]  # not connected
  J12 = female pin header, 5 pins [form="♀ (female)"]  # not connected
  J13 = female pin header, 5 pins [form="♀ (female)"]  # not connected
  J14 = female pin header, 5 pins [form="♀ (female)"]  # not connected

nets:
  GND: Part1.GND, S2.O, J2.pin5, Adafruit_HUZZAH_ESP8266_Breakout1.GND
  N1: Part1.D0/RX, S1.3, S1.4
  N2: Part1.D1/TX, S1.1, S1.6
  N3: Part1.RESET, S2.P
  N4: Part1.5V, Adafruit_HUZZAH_ESP8266_Breakout1.VBat, Adafruit_HUZZAH_ESP8266_Breakout1.V+
  N5: S1.2, Adafruit_HUZZAH_ESP8266_Breakout1.TX
  N6: S1.5, Adafruit_HUZZAH_ESP8266_Breakout1.RX
  N7: J1.pin1, Adafruit_HUZZAH_ESP8266_Breakout1.#5
  N8: J1.pin2, Adafruit_HUZZAH_ESP8266_Breakout1.#4
  N9: J1.pin3, Adafruit_HUZZAH_ESP8266_Breakout1.#0
  N10: J1.pin4, Adafruit_HUZZAH_ESP8266_Breakout1.#2
  N11: J1.pin5, Adafruit_HUZZAH_ESP8266_Breakout1.#15
  N12: J1.pin6, Adafruit_HUZZAH_ESP8266_Breakout1.3V
  N13: J2.pin1, Adafruit_HUZZAH_ESP8266_Breakout1.#13
  N14: J2.pin2, Adafruit_HUZZAH_ESP8266_Breakout1.#12
  N15: J2.pin3, Adafruit_HUZZAH_ESP8266_Breakout1.#14
  N16: J2.pin4, Adafruit_HUZZAH_ESP8266_Breakout1.#16

notes:
  Particle Shield
  rXTX
  Huzzah 8266
  15  2  0  4  5
  3V3
  1    2
  13  12  14  16  GND
  Designed in the UK
  Protoboard
